# Fritzing sketch NanoMeetPIR+DHT+Pi Kopie (saved by Fritzing 0.9.3b)
breadboards: 1

parts:
  Raspberry_Pi_Zero1 = Raspberry Pi Zero
  PIR2 = PIR sensor
  R1 = Resistor [tolerance=±5% resistance=10k package=THT]
  LED1 = LED - 5mm [color="Green (555nm)" package="5 mm [THT]"]
  RHT1 = Humidity and Temperature Sensor RHT03
  R2 = Resistor [tolerance=±5% resistance=10k package=THT]
  S1 = Pushbutton [package="[THT]"]

nets:
  3V3: Raspberry_Pi_Zero1.3v3, RHT1.Vcc, R2.Pin_0
  N1: Raspberry_Pi_Zero1.GPIO3, S1.Pin_1, S1.Pin_2
  N2: Raspberry_Pi_Zero1.GPIO4, RHT1.Data-signal, R2.Pin_1
  N3: Raspberry_Pi_Zero1.GPIO17, PIR2.SIG
  N4: Raspberry_Pi_Zero1.GPIO27, R1.Pin_0
  GND: Raspberry_Pi_Zero1.GND, PIR2.GND, LED1.cathode, RHT1.GND_2, S1.Pin_3, S1.Pin_4
  5V: Raspberry_Pi_Zero1.5V, PIR2.VDD
  N5: R1.Pin_1, LED1.anode
